// Logisim project ALU.circ as structural Verilog: 1 circuit, main circuit main
module main (
  input  [3:0] X,
  input  [3:0] Y,
  input  ZY,
  input  ZX,
  input  NY,
  input  NX,
  input  AND_ADD,
  input  NO,
  output [3:0] out_9,
  output ZO
);

  wire or_1_out;
  wire [3:0] adder_1_out, and_1_out, multiplexer_1_out, multiplexer_2_out, multiplexer_3_out,
       multiplexer_4_out, multiplexer_5_out, not_1_out, not_2_out, not_3_out;

  Multiplexer #(.width(4), .enable("false")) multiplexer_1 (.in0(X), .in1(4'b0000), .out(multiplexer_1_out), .sel(ZX));
  Multiplexer #(.width(4), .enable("false")) multiplexer_2 (.in0(Y), .in1(4'b0000), .out(multiplexer_2_out), .sel(ZY));
  // Probe on multiplexer_1_out
  Multiplexer #(.width(4), .enable("false")) multiplexer_3 (
    .in0(multiplexer_1_out), .in1(not_1_out), .out(multiplexer_3_out), .sel(NX));
  assign not_1_out = ~multiplexer_1_out;  // NOT_Gate not_1, 4 bits wide
  Multiplexer #(.width(4), .enable("false")) multiplexer_4 (
    .in0(multiplexer_2_out), .in1(not_2_out), .out(multiplexer_4_out), .sel(NY));
  assign not_2_out = ~multiplexer_2_out;  // NOT_Gate not_2, 4 bits wide
  // Probe on multiplexer_3_out
  assign and_1_out = multiplexer_4_out & multiplexer_3_out;  // AND_Gate and_1, 4 bits wide
  Adder #(.width(4)) adder_1 (.a(multiplexer_4_out), .b(multiplexer_3_out), .out(adder_1_out));  // open: cin, cout
  // Probe on multiplexer_5_out
  Multiplexer #(.width(4), .enable("false")) multiplexer_5 (
    .in0(and_1_out), .in1(adder_1_out), .out(multiplexer_5_out), .sel(AND_ADD));
  Multiplexer #(.width(4), .enable("false")) multiplexer_6 (
    .in0(multiplexer_5_out), .in1(not_3_out), .out(out_9), .sel(NO));
  assign not_3_out = ~multiplexer_5_out;  // NOT_Gate not_3, 4 bits wide
  or or_1 (or_1_out, out_9[0], out_9[1], out_9[2], out_9[3]);
  not not_4 (ZO, or_1_out);
endmodule
