// Logisim project Full_Adder_Circ.circ as structural Verilog: 2 circuits, main circuit main
module main (
  input  in_1,
  input  in_2,
  input  _1,
  input  _1_2,
  input  Cin,
  input  _2,
  input  _2_2,
  input  _3,
  input  _3_2,
  input  _4,
  input  _4_2,
  input  _1_3,
  input  _1_4,
  input  _2_3,
  input  _2_4,
  input  _3_3,
  input  _3_4,
  input  _4_3,
  input  _4_4,
  output out_20,
  output out_21,
  output _1_5,
  output _2_5,
  output _3_5,
  output _4_5,
  output Cout,
  output _1_6,
  output _2_6,
  output _3_6,
  output _4_6,
  output Cout_2
);

  xor xor_1 (out_20, in_1, in_2);
  and and_1 (out_21, in_1, in_2);
  Full_Adder full_adder_1 (
    .A1(_1), .B1(_1_2), .Cin(Cin), .A2(_2), .B2(_2_2), .A3(_3), .A4(_4), .B4(_4_2), .S4(_4_5), .Cout(Cout),
    .B3(_3_2), .S1(_1_5), .S2(_2_5), .S3(_3_5));
  Full_Adder full_adder_2 (
    .A1(_1_3), .B1(_1_4), .Cin(Cout), .A2(_2_3), .B2(_2_4), .A3(_3_3), .A4(_4_3), .B4(_4_4), .S4(_4_6),
    .Cout(Cout_2), .B3(_3_4), .S1(_1_6), .S2(_2_6), .S3(_3_6));
endmodule

// 4bit Full Adder
module Full_Adder (
  input  A1,
  input  B1,
  input  Cin,
  input  A2,
  input  B2,
  input  A3,
  input  B3,
  input  A4,
  input  B4,
  output S1,
  output S2,
  output S3,
  output S4,
  output Cout
);

  wire and_1_out, and_2_out, and_3_out, and_4_out, and_5_out, and_6_out, and_7_out, and_8_out, or_1_out,
       or_2_out, or_3_out, xor_1_out, xor_2_out, xor_3_out, xor_4_out;

  xor xor_1 (xor_1_out, A1, B1);
  and and_1 (and_1_out, A1, B1);
  xor xor_2 (xor_2_out, A2, B2);
  and and_2 (and_2_out, A2, B2);
  xor xor_3 (xor_3_out, A3, B3);
  and and_3 (and_3_out, A3, B3);
  xor xor_4 (xor_4_out, A4, B4);
  and and_4 (and_4_out, A4, B4);
  xor xor_5 (S1, xor_1_out, Cin);
  and and_5 (and_5_out, xor_1_out, Cin);
  xor xor_6 (S2, xor_2_out, or_1_out);
  and and_6 (and_6_out, xor_2_out, or_1_out);
  xor xor_7 (S3, xor_3_out, or_2_out);
  and and_7 (and_7_out, xor_3_out, or_2_out);
  xor xor_8 (S4, xor_4_out, or_3_out);
  and and_8 (and_8_out, xor_4_out, or_3_out);
  or or_1 (or_1_out, and_5_out, and_1_out);
  or or_2 (or_2_out, and_6_out, and_2_out);
  or or_3 (or_3_out, and_7_out, and_3_out);
  or or_4 (Cout, and_8_out, and_4_out);
endmodule
