// Logisim project RAM2to4.circ as structural Verilog: 2 circuits, main circuit main
module main (
  input  in_1,
  input  in_2,
  input  in_3,
  input  in_4,
  input  in_5,
  input  in_6,
  input  in_7,
  input  in_8,
  input  in_9,
  output out_10,
  output out_11,
  output out_12,
  output out_13,
  output out_14,
  output out_15,
  output out_16,
  output out_17
);

  wire clock_1_out, clock_2_out, counter_1_q, demultiplexer_1_out0, demultiplexer_1_out1,
       demultiplexer_2_out0, demultiplexer_2_out1, demultiplexer_3_out0, demultiplexer_3_out1,
       demultiplexer_4_out0, demultiplexer_4_out1, demultiplexer_5_out0, demultiplexer_5_out1,
       multiplexer_2_out, multiplexer_3_out;
  wire [1:0] counter_2_q;

  Clock clock_1 (.out(clock_1_out));
  BIT BIT (.IN(in_1), .CLK(in_2), .OUT(out_10));
  Demultiplexer #(.enable("false")) demultiplexer_1 (
    .out0(demultiplexer_1_out0), .out1(demultiplexer_1_out1), .in(clock_1_out), .sel(counter_1_q));
  Counter #(.width(1), .max('h1)) counter_1 (.Q(counter_1_q), .clk(clock_1_out));  // open: load, D, count, carry, clr
  Multiplexer #(.enable("false")) multiplexer_1 (.in0(out_11), .in1(in_3), .out(out_11), .sel(in_4));
  Multiplexer #(.enable("false")) multiplexer_2 (.in0(in_5), .in1(in_6), .out(multiplexer_2_out), .sel(counter_1_q));
  D_Flip_Flop d_ff_1 (.clk(demultiplexer_1_out0), .D(multiplexer_2_out), .Q(out_12));  // open: Qn, preset, en, reset
  D_Flip_Flop d_ff_2 (.clk(demultiplexer_1_out1), .D(multiplexer_2_out), .Q(out_14));  // open: Qn, preset, en, reset
  Counter #(.width(2), .max('h3)) counter_2 (.Q(counter_2_q), .clk(clock_2_out));  // open: load, D, count, carry, clr
  Clock clock_2 (.out(clock_2_out));
  Demultiplexer #(.enable("false")) demultiplexer_2 (
    .out0(demultiplexer_2_out0), .out1(demultiplexer_2_out1), .in(clock_2_out), .sel(counter_2_q[0]));
  Multiplexer #(.enable("false")) multiplexer_3 (.in0(in_7), .in1(in_8), .out(multiplexer_3_out), .sel(counter_2_q[0]));
  Demultiplexer #(.enable("false")) demultiplexer_3 (
    .out0(demultiplexer_3_out0), .out1(demultiplexer_3_out1), .in(demultiplexer_2_out0), .sel(in_9));
  Demultiplexer #(.enable("false")) demultiplexer_4 (
    .out0(demultiplexer_4_out0), .out1(demultiplexer_4_out1), .in(demultiplexer_2_out1), .sel(in_9));
  Demultiplexer #(.enable("false")) demultiplexer_5 (
    .out0(demultiplexer_5_out0), .out1(demultiplexer_5_out1), .in(multiplexer_3_out), .sel(counter_2_q[0]));
  D_Flip_Flop d_ff_3 (.clk(demultiplexer_3_out0), .D(demultiplexer_5_out0), .Q(out_13));  // open: Qn, preset, en, reset
  D_Flip_Flop d_ff_4 (.clk(demultiplexer_3_out1), .D(demultiplexer_5_out0), .Q(out_15));  // open: Qn, preset, en, reset
  D_Flip_Flop d_ff_5 (.clk(demultiplexer_4_out0), .D(demultiplexer_5_out1), .Q(out_16));  // open: Qn, preset, en, reset
  D_Flip_Flop d_ff_6 (.clk(demultiplexer_4_out1), .D(demultiplexer_5_out1), .Q(out_17));  // open: Qn, preset, en, reset
endmodule

module BIT (
  input  IN,
  input  CLK,
  output OUT
);

  wire nand_1_out, nand_2_out, nand_4_out, not_1_out;

  not not_1 (not_1_out, IN);
  nand nand_1 (nand_1_out, IN, CLK);
  nand nand_2 (nand_2_out, CLK, not_1_out);
  nand nand_3 (OUT, nand_1_out, nand_4_out);
  nand nand_4 (nand_4_out, OUT, nand_2_out);
endmodule
